// Logisim project projefinal.circ as structural Verilog: 2 circuits, main circuit main
module main (
  input  Reset,
  output [7:0] Register0,
  output [7:0] Register1,
  output [7:0] Register2,
  output [7:0] Register3,
  output [7:0] Register4,
  output [7:0] Register5,
  output [7:0] Register6,
  output [7:0] Register7,
  output [1:0] Cycle_Counter
);

  wire and_1_out, and_2_out, and_3_out, and_4_out, and_5_out, clock_1_out, decoder_1_out0, decoder_1_out1,
       decoder_1_out2, decoder_1_out3, decoder_1_out4, decoder_1_out5, decoder_1_out6, decoder_1_out7,
       nand_1_out, not_1_out, not_2_out, not_3_out, not_4_out, not_5_out, not_6_out, or_1_out;
  wire [1:0] adder_1_out, multiplexer_5_out;
  wire [3:0] counter_1_q, multiplexer_1_out, multiplexer_2_out, multiplexer_3_out;
  wire [7:0] A_q, alu_1_out_4, B_q, multiplexer_4_out, register_1_q, rom_1_data;

  Counter #(.width(4), .max('hf)) counter_1 (.Q(counter_1_q), .clk(and_1_out));  // open: load, D, count, carry, clr
  Clock clock_1 (.out(clock_1_out));
  ROM #(.addrWidth(4)) rom_1 (.addr(counter_1_q), .data(rom_1_data));  // open: sel
  and and_1 (and_1_out, clock_1_out, and_2_out);
  Register R0 (.D(multiplexer_4_out), .en(decoder_1_out0), .Q(Register0), .clk(clock_1_out), .clr(Reset));
  and and_2 (and_2_out, not_1_out, not_2_out);
  Register R1 (.D(multiplexer_4_out), .en(decoder_1_out1), .Q(Register1), .clk(clock_1_out), .clr(Reset));
  Register register_1 (.D(rom_1_data), .en(and_2_out), .Q(register_1_q), .clk(clock_1_out), .clr(Reset));
  not not_1 (not_1_out, Cycle_Counter[1]);
  not not_2 (not_2_out, Cycle_Counter[0]);
  Register R2 (.D(multiplexer_4_out), .en(decoder_1_out2), .Q(Register2), .clk(clock_1_out), .clr(Reset));
  not not_3 (not_3_out, register_1_q[7]);
  Register R3 (.D(multiplexer_4_out), .en(decoder_1_out3), .Q(Register3), .clk(clock_1_out), .clr(Reset));
  Register R4 (.D(multiplexer_4_out), .en(decoder_1_out4), .Q(Register4), .clk(clock_1_out), .clr(Reset));
  Multiplexer #(.width(4)) multiplexer_1 (
    .in0({1'b0, register_1_q[2:0]}), .in1({register_1_q[6], 3'b000}), .out(multiplexer_1_out),
    .sel(register_1_q[6]), .en(not_3_out));
  Register R5 (.D(multiplexer_4_out), .en(decoder_1_out5), .Q(Register5), .clk(clock_1_out), .clr(Reset));
  Register R6 (.D(multiplexer_4_out), .en(decoder_1_out6), .Q(Register6), .clk(clock_1_out), .clr(Reset));
  Decoder #(.select(3), .disabled(0)) decoder_1 (
    .out0(decoder_1_out0), .out1(decoder_1_out1), .out2(decoder_1_out2), .out3(decoder_1_out3),
    .out4(decoder_1_out4), .out5(decoder_1_out5), .out6(decoder_1_out6), .out7(decoder_1_out7),
    .sel(register_1_q[5:3]), .en(or_1_out));
  Multiplexer #(.width(4), .enable("false")) multiplexer_2 (
    .in0({1'b0, register_1_q[5:3]}), .in1(multiplexer_1_out), .out(multiplexer_2_out), .sel(not_3_out));
  Register R7 (.D(multiplexer_4_out), .en(decoder_1_out7), .Q(Register7), .clk(clock_1_out), .clr(Reset));
  Multiplexer #(.select(2), .width(4), .enable("false")) multiplexer_3 (
    .in1(multiplexer_2_out), .in2({1'b0, register_1_q[2:0]}), .in3(4'b1001), .out(multiplexer_3_out),
    .sel(Cycle_Counter));  // open: in0
  Multiplexer #(.select(4), .width(8), .enable("false")) multiplexer_4 (
    .in0(Register0), .in1(Register1), .in2(Register2), .in3(Register3), .in4(Register4), .in5(Register5),
    .in6(Register6), .in7(Register7), .in8(rom_1_data), .in9(B_q), .out(multiplexer_4_out),
    .sel(multiplexer_3_out));  // open: in10, in11, in12, in13, in14, in15
  Register A (.D(multiplexer_4_out), .en(and_3_out), .Q(A_q), .clk(clock_1_out), .clr(Reset));
  ALU alu_1 (.out_4(alu_1_out_4), .in_3(register_1_q[6]), .in_2(multiplexer_4_out), .in_1(A_q));
  Register B (.D(alu_1_out_4), .en(nand_1_out), .Q(B_q), .clk(clock_1_out), .clr(Reset));
  LED DONE (.in(or_1_out));
  or or_1 (or_1_out, and_4_out, and_5_out);
  and and_3 (and_3_out, not_4_out, Cycle_Counter[0]);
  nand nand_1 (nand_1_out, Cycle_Counter[1], Cycle_Counter[0]);
  and and_4 (and_4_out, not_5_out, Cycle_Counter[0], not_3_out);
  and and_5 (and_5_out, Cycle_Counter[1], not_6_out, Cycle_Counter[0]);
  Adder #(.width(2)) adder_1 (.a(2'b01), .b(Cycle_Counter), .out(adder_1_out));  // open: cin, cout
  not not_4 (not_4_out, Cycle_Counter[1]);
  not not_5 (not_5_out, Cycle_Counter[1]);
  not not_6 (not_6_out, not_3_out);
  Register #(.width(2)) register_2 (
    .D(multiplexer_5_out), .Q(Cycle_Counter), .clk(clock_1_out), .clr(Reset));  // open: en
  Multiplexer #(.width(2), .enable("false")) multiplexer_5 (
    .in0(adder_1_out), .in1(2'b00), .out(multiplexer_5_out), .sel(or_1_out));
  // Probe on nothing
  // Probe on nothing

  // Notes on the sheet:
  //   contents of rom_1 (hex, n*v repeats v):
  //   68 b8 35 0 68 6f b5 0 ad 0 ee
endmodule

module ALU (
  input  [7:0] in_1,
  input  [7:0] in_2,
  input  in_3,
  output [7:0] out_4
);

  wire [7:0] adder_1_out, subtractor_1_out;

  Adder adder_1 (.a(in_1), .b(in_2), .out(adder_1_out));  // open: cin, cout
  Subtractor subtractor_1 (.a(in_1), .b(in_2), .out(subtractor_1_out));  // open: bin, bout
  Multiplexer #(.width(8), .enable("false")) multiplexer_1 (
    .in0(adder_1_out), .in1(subtractor_1_out), .out(out_4), .sel(in_3));
endmodule
